# Fritzing sketch Sketches (saved by Fritzing 0.9.3b)
breadboards: 1

parts:
  Part1 = Arduino Uno (Rev3)
  S2 = Pushbutton [package="[THT]"]
  LED1 = LED - 5mm [color="Red (633nm)" package="5 mm [THT]"]
  R1 = Resistor [tolerance=±5% resistance=10k package=THT]
  S3 = Pushbutton [package="[THT]"]

nets:
  N1: Part1.GND, S2.Pin_3, S2.Pin_4, LED1.cathode, S3.Pin_3, S3.Pin_4
  N2: Part1.D5_PWM, R1.Pin_1
  N3: Part1.D6_PWM, S3.Pin_1, S3.Pin_2
  N4: Part1.D7, S2.Pin_1, S2.Pin_2
  N5: LED1.anode, R1.Pin_0
